# Fritzing sketch AVL Schematic (saved by Fritzing 0.9.3b)
breadboards: 1

parts:
  U1 = atmega328 [package=dip]
  U2 = Voltage Regulator - 5V [package="DPak [SMD]"]
  LED1 = LED - 3mm [color="Green (565nm)" package="3 mm [THT]"]
  LED2 = LED - 3mm [color="Red (633nm)" package="3 mm [THT]"]
  R1 = Resistor [tolerance=±5% resistance=220 package="0603 [SMD]"]
  R2 = Resistor [tolerance=±5% resistance=220 package="0603 [SMD]"]
  R3 = Resistor [tolerance=±5% resistance=10k package="0603 [SMD]"]
  C3 = Electrolytic Capacitor [capacitance=10µF package="200 mil [THT, electrolytic]"]
  C4 = Electrolytic Capacitor [capacitance=10µF package="200 mil [THT, electrolytic]"]
  C5 = Ceramic Capacitor [capacitance=22pF package="100 mil [THT, multilayer]"]
  C6 = Ceramic Capacitor [capacitance=22pF package="100 mil [THT, multilayer]"]
  S1 = Pushbutton [package="[SMD]"]
  GSM_SIM_GPSR_SMS_SIM900_SIM1 = SIM800L [package=THT]
  U3 = microSD Socket [package="112-TXAR-R01 [SMD]"]
  Part1 = u-blox NEO-6M GPS Breakout
  LED4 = LED - 3mm [color="Blue (430nm)" package="3 mm [THT]"]
  R4 = Resistor [tolerance=±5% resistance=220 package="0603 [SMD]"]
  XTAL3 = Crystal [frequency="16 Mhz" package=THT]

nets:
  N1: U1.RESET, R3.Pin_0, S1.Pin_1, S1.Pin_2
  N2: U1.D0_(RX), Part1.TXD
  N3: U1.D2, GSM_SIM_GPSR_SMS_SIM900_SIM1.SIM_RXD
  N4: U1.D3_(PWM), GSM_SIM_GPSR_SMS_SIM900_SIM1.SIM_TXD
  N5: U1.D4, GSM_SIM_GPSR_SMS_SIM900_SIM1.RST
  VCC: U1.VCC, U1.AVCC, U1.AREF, U2.output_voltage, R2.Pin_1, R3.Pin_1, C3.-, U3.VCC
  GND: U1.GND, U2.GND, LED2.cathode, R1.Pin_0, C3.+, C4.+, C5.0, C6.1, S1.Pin_3, S1.Pin_4, GSM_SIM_GPSR_SMS_SIM900_SIM1.GND, U3.GND, Part1.GND, R4.Pin_1
  N6: U1.XLAT1, C5.1, XTAL3.pin_0
  N7: U1.XLAT2, C6.0, XTAL3.pin_1
  N8: U1.D7, LED4.anode
  N9: U1.D10_(PWM), U3.CS
  N10: U1.D11_(PWM), U3.DI
  N11: U1.D12, U3.DO
  N12: U1.D13, LED1.anode, U3.SCK
  N13: U2.input_voltage, C4.-
  N14: LED1.cathode, R1.Pin_1
  N15: LED2.anode, R2.Pin_0
  N16: LED4.cathode, R4.Pin_0

notes:
  5V
  3.8V
  3.3V
  12V
  Connection LED

custom parts:
  microSD Socket: 112-TXAR-R01 microSD socket.
